# Fritzing sketch HM_10_BT (saved by Fritzing 0.9.3b)
breadboards: 2

parts:
  Part1 = Bluetooth HM-10
  Part3 = Arduino Uno (Rev3) - ICSP
  R1 = Resistor [tolerance=±5% resistance=1k package=THT]
  R2 = Resistor [tolerance=±5% resistance=2.2k package=THT]
  Part4 = Arduino Uno (Rev3) - ICSP
  Part5 = Bluetooth HM-10
  R3 = Resistor [tolerance=±5% resistance=1k package=THT]
  R4 = Resistor [tolerance=±5% resistance=2.2k package=THT]
  R5 = Photocell (LDR) [package=THT]
  R6 = Resistor [tolerance=±5% resistance=10k package=THT]

nets:
  N1: Part1.RXD, R1.Pin_0, R2.Pin_1
  N2: Part1.TXD, Part3.D10_PWM/SS
  GND: Part1.GND, Part3.GND, R2.Pin_0, R6.Pin_0
  VCC: Part1.VCC, Part3.5V, R5.pin_0
  N3: Part3.A0, R5.pin_1, R6.Pin_1
  N4: Part3.ICSP_MOSI, Part3.D11_PWM/MOSI, R1.Pin_1
  N5: Part4.ICSP_MOSI, Part4.D11_PWM/MOSI, R3.Pin_1
  N6: Part4.D10_PWM/SS, Part5.TXD
  5V: Part4.5V, Part5.VCC
  GND_2: Part4.GND, Part5.GND, R4.Pin_0
  N7: Part5.RXD, R3.Pin_0, R4.Pin_1
